# Fritzing sketch waveglide (saved by Fritzing 0.9.2b)
circuit board: 6cm x 16cm

parts:
  ChargeBooster = PowerBoost 500 Charger
  Trinket = Pro Trinket 5V
  BMP180 = BMP085 Breakout
  BATT1 = LiPoly Battery (1300mAh)
  Buzzer = Piezo Speaker
  MXPV7002G = IC, DIP package, 8 pins [chip_label=MXPV7002G]
  SSR = IC, DIP package, 4 pins [chip_label=SSR]
  12V_Booster = female pin header, 3 pins [form="♀ (female)"]
  R2 = Resistor [tolerance=±5% resistance=330 package=THT]
  EValve = Solenoid
  D1 = Rectifier Diode [part_number=1N4001 package="300 mil [THT]"]
  OLED1 = 1.27" 128x96 16-bit OLED Breakout  # not connected
  DisplayHeader = female pin header, 11 pins [form="♀ (female)"]
  SSR1 = IC, DIP package, 6 pins [chip_label=IC]
  SSR2 = IC, DIP package, 6 pins [chip_label=IC]
  R3 = Resistor [tolerance=±5% resistance=330 package=THT]
  R4 = Resistor [tolerance=±5% resistance=330 package=THT]
  C1 = Ceramic Capacitor [capacitance=1µF voltage=20V package="100 mil [THT, multilayer]"]
  C2 = Ceramic Capacitor [capacitance=0.01µF voltage=20V package="100 mil [THT, multilayer]"]
  C3 = Ceramic Capacitor [capacitance=470pF voltage=20V package="100 mil [THT, multilayer]"]
  EValve1 = female pin header, 1 pin [form="♀ (female)"]
  EValve2 = female pin header, 1 pin [form="♀ (female)"]
  TheMotherOfButtons = SWITCH-MOMENTARY-2 [package=tactile-pth-12mm]

nets:
  N1: ChargeBooster.VBAT, 12V_Booster.pin3, SSR1.pin5, SSR2.pin5
  GND: ChargeBooster.GND, Trinket.GND, BMP180.GND, BATT1.negative, Buzzer.pin1, MXPV7002G.pin3, SSR.pin2, 12V_Booster.pin2, EValve.pin1, D1.anode, DisplayHeader.pin11, C1.0, C2.0, C3.0, EValve1.pin1, TheMotherOfButtons.1
  N2: ChargeBooster.5.0V, Trinket.VBUS, BMP180.VIN, MXPV7002G.pin2, DisplayHeader.pin10, C1.1, C2.1
  N3: Trinket.D8, DisplayHeader.pin3
  N4: Trinket.D6, SSR2.pin2
  N5: Trinket.D5, SSR1.pin2, TheMotherOfButtons.2
  N6: Trinket.D4, DisplayHeader.pin6
  N7: Trinket.D3, Buzzer.pin2
  N8: Trinket.D9, DisplayHeader.pin4
  N9: Trinket.D10, DisplayHeader.pin5
  N10: Trinket.D11, DisplayHeader.pin1
  N11: Trinket.D12, DisplayHeader.pin7, DisplayHeader.pin8
  N12: Trinket.D13, DisplayHeader.pin2
  N13: Trinket.A0, R2.Pin_0
  N14: Trinket.A3, MXPV7002G.pin4, C3.1
  N15: Trinket.A4, BMP180.SDA
  N16: Trinket.A5, BMP180.SCL
  N17: BATT1.positive, SSR1.pin4, SSR1.pin6, SSR2.pin4, SSR2.pin6, R3.Pin_0, R4.Pin_0
  N18: SSR.pin1, R2.Pin_1
  N19: SSR.pin3, EValve.pin2, D1.cathode, EValve2.pin1
  N20: SSR.pin4, 12V_Booster.pin1
  N21: SSR1.pin1, R3.Pin_1
  N22: SSR2.pin1, R4.Pin_1

notes:
  micro USB charging
  power LED
  low bat LED
  charging LED
  full LED
  12V booster
  O2 IN
  O2 OUT
  WaveGlide
  Alpha-01
  Nortd Labs 2015

custom parts:
  PowerBoost 500 Charger: The PowerBoost 500C is a little DC/DC boost converter module that can be powered by any 3.7V LiIon/LiPoly battery, and convert the battery output to 5.2V DC for running your 5V projects. At its heart is a TPS61090 boost converter from TI. This boost converter chip has some really nice extras such as low battery detection, 2A internal switch, synchronous conversion, excellent efficiency, and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
  Pro Trinket 5V: The Pro Trinket 5V is like an Arduino Pro Mini with more pins and USB included. Built with the common core Arduino chip, the ATmega328p, it has 18 GPIO, 2 extra analog inputs, 28K of flash, and 2K of RAM. It has onboard USB bootloading support with Optiboot support, so you can either program your Pro Trinket over USB or with a FTDI cable. The Pro Trinket is programmable using the Arduino IDE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
  BMP085 Breakout: A breakout for the BMP085 barometric pressure and temperature sensor
  LiPoly Battery (1300mAh): Lithium Ion Polymer Battery (1300mAh)
